// Logisim project Relatório 1.circ as structural Verilog
module _1__Identidade_da_Soma__OR (
  input  in_1,
  output out_2
);

  or or_1 (out_2, in_1, 1'b0);
endmodule

module _2__Elemento_Neutro_da_Soma__OR (
  input  in_1,
  output out_2
);

  or or_1 (out_2, in_1, 1'b1);
endmodule

module \_3__Idempotência_da_Soma__OR  (
  input  in_1,
  output out_2
);

  or or_1 (out_2, in_1, in_1);
endmodule

module \_4__Princípio_da_Complementação__OR___NOT  (
  input  in_1,
  output out_2
);

  wire not_1_out;

  not not_1 (not_1_out, in_1);
  or or_1 (out_2, in_1, not_1_out);
endmodule

module \_5__Elemento_Nulo_da_Multiplicação__AND  (
  input  in_1,
  output out_2
);

  and and_1 (out_2, in_1, 1'b0);
endmodule

module \_6__Elemento_Neutro_da_Multiplicação__AND  (
  input  in_1,
  output out_2
);

  and and_1 (out_2, in_1, 1'b1);
endmodule

module \_7__Idempotência_da_Multiplicação__AND  (
  input  in_1,
  output out_2
);

  and and_1 (out_2, in_1, in_1);
endmodule

module \_8__Princípio_da_Complementação__AND___NOT  (
  input  in_1,
  output out_2
);

  wire not_1_out;

  not not_1 (not_1_out, in_1);
  and and_1 (out_2, in_1, not_1_out);
endmodule

module \_9__Absorção__OR___AND  (
  input  in_1,
  input  in_2,
  output out_3
);

  wire and_1_out;

  and and_1 (and_1_out, in_1, in_2);
  or or_1 (out_3, in_1, and_1_out);
endmodule

module \_10__Teorema_da_Absorção__AND___OR___NOT  (
  input  in_1,
  input  in_2,
  output out_3
);

  wire and_1_out, and_2_out, not_1_out;

  not not_1 (not_1_out, in_2);
  and and_1 (and_1_out, in_1, in_2);
  and and_2 (and_2_out, not_1_out, in_1);
  or or_1 (out_3, and_1_out, and_2_out);
endmodule

module \_11__Aprovação_de_Aluno  (
  input  in_1,
  input  in_2,
  input  in_3,
  output out_4
);

  wire or_1_out;

  or or_1 (or_1_out, in_2, in_3);
  and and_1 (out_4, in_1, or_1_out);
endmodule

module _12__Sistema_de_Alarme (
  input  in_1,
  input  in_2,
  input  in_3,
  output out_4
);

  wire and_1_out, and_2_out, not_1_out;

  not not_1 (not_1_out, in_3);
  and and_1 (and_1_out, in_2, not_1_out);
  and and_2 (and_2_out, in_2, and_1_out);
  or or_1 (out_4, in_1, and_2_out);
endmodule
